# Fritzing sketch Circuit (saved by Fritzing 0.9.3b)

parts:
  Part1 = Arduino Nano (Rev3.0)
  J1 = screw terminal, 2 pins
  U1 = ESP8266 WiFi Module [part_number=ESP8266]
  Part2 = ACS712 Low Current Sensor Board v12
  LCD1 = LCD screen
  LCM1602_IIC1 = LCM1602 IIC [part_number="LCM1602 IIC" chip_label="LCM1602 IIC" package="DIP (Dual Inline) [THT]"]
  T1 = LM35 Temperature Sensor [package="TO92 [THT]"]
  8_Channel_Relay1 = 8 Channel Power Relay

nets:
  GND: Part1.GND, U1.GND
  N1: Part1.D2, U1.TXD
  N2: Part1.D3, U1.RXD
  N3: Part1.D5, 8_Channel_Relay1.IN8
  N4: Part1.D6, 8_Channel_Relay1.IN7
  N5: Part1.D7, 8_Channel_Relay1.IN6
  N6: Part1.D8, 8_Channel_Relay1.IN5
  N7: Part1.D9, 8_Channel_Relay1.IN4
  N8: Part1.D10, 8_Channel_Relay1.IN3
  N9: Part1.D11/MOSI, 8_Channel_Relay1.IN2
  N10: Part1.D12/MISO, 8_Channel_Relay1.IN1
  N11: Part1.A7, Part2.VO
  N12: Part1.A6, T1.Vout
  N13: Part1.A5, LCM1602_IIC1.SCL
  N14: Part1.A4, LCM1602_IIC1.SDA
  3V3: Part1.3V3, U1.VCC, U1.CH_PD
  VCC: J1.pin1, Part2.5V, LCM1602_IIC1.VCC, T1.+Vs, 8_Channel_Relay1.VCC
  GND_2: J1.pin2, Part2.GND, LCM1602_IIC1.GND, T1.GND, 8_Channel_Relay1.GND
  VSS: LCD1.VSS, LCM1602_IIC1.VSS
  VDD: LCD1.VDD, LCM1602_IIC1.VDD
  N15: LCD1.V0, LCM1602_IIC1.V0
  N16: LCD1.RS, LCM1602_IIC1.RS
  N17: LCD1.R/W, LCM1602_IIC1.RW
  N18: LCD1.E, LCM1602_IIC1.E
  N19: LCD1.DB0, LCM1602_IIC1.D0
  N20: LCD1.DB1, LCM1602_IIC1.D1
  N21: LCD1.DB2, LCM1602_IIC1.D2
  N22: LCD1.DB3, LCM1602_IIC1.D3
  N23: LCD1.DB4, LCM1602_IIC1.D4
  N24: LCD1.DB5, LCM1602_IIC1.D5
  N25: LCD1.DB6, LCM1602_IIC1.D6
  N26: LCD1.DB7, LCM1602_IIC1.D7
  N27: LCD1.LED+, LCM1602_IIC1.A
  N28: LCD1.LED-, LCM1602_IIC1.K

notes:
  5 VOLTS
  RELAY BOARD
  16X2 LCD
  I2C ADAPTER FOR LCD
  ARDUINO NANO
  ESP8266-01
  LM35
  CURRENT SENSOR

custom parts:
  ESP8266 WiFi Module: Generic WiFi Module based on the ESP8266 with onboard PCB antenna and UART communications
  LCM1602 IIC: I2C-Module to use a 1602 or 2004 LCD on with the wire.h libory Serial LCD Modul
  8 Channel Power Relay: An 8 channel power relay. The module operates at 5V.
